# Fritzing sketch Circuit Diagram (saved by Fritzing 0.9.3b)

parts:
  M1 = DC Motor
  M3 = DC Motor
  M4 = DC Motor
  Tiva_C_LaunchPad1 = Tiva C TM4C123G [package=THT]
  S1 = H-Bridge with L298N
  M2 = DC Motor
  Part1 = Bluetooth HC-05 Macho
  hc-sr1 = hc-sr04
  VCC1 = 4 x AAA Battery Mount

nets:
  N1: M1.pin_1, M2.pin_1
  N2: M1.pin_2, M2.pin_2
  N3: M3.pin_1, M4.pin_1
  N4: M3.pin_2, M4.pin_2
  N5: Tiva_C_LaunchPad1.PB0, S1.IN1
  N6: Tiva_C_LaunchPad1.PB1, S1.IN2
  N7: Tiva_C_LaunchPad1.PD0, hc-sr1.Echo
  N8: Tiva_C_LaunchPad1.PD1, hc-sr1.Trig
  N9: Tiva_C_LaunchPad1.PB3, S1.IN4
  N10: Tiva_C_LaunchPad1.PB2, S1.IN3
  N11: Tiva_C_LaunchPad1.PB7, Part1.TXD
  N12: Tiva_C_LaunchPad1.PB6, Part1.RXD
  N13: S1.12V, VCC1.+
  N14: S1.GND, VCC1.-
  VCC: Part1.VCC, hc-sr1.VCC
  GND: Part1.GND, hc-sr1.GND

notes:
  Group Members:
  Ghulam Samdani (2018-EE-285)
  Husnain Abdullah (2018-EE-288)
  Muhammad Umer (2018-EE-290)
  Circuit Diagram of Voice Controlled Car using TIVA C
  Left Side
  Right Side

custom parts:
  Tiva C TM4C123G: Tiva C LaunchPad EK-TM4C123GXL
  H-Bridge with L298N: h-bridge
